// Digital circuit Lobinho.dig as structural Verilog
module Lobinho (
  input  clk,
  output [2:0] out_2,
  output [4:0] out_3
);

  wire button_6_out, button_7_out, button_8_out, button_9_out, u_PoliLobinho_db_clock;
  wire [4:0] button_1_out;
  wire [6:0] not_1_out, not_2_out, not_3_out, not_4_out, not_5_out, not_6_out, u_PoliLobinho_db_atacado_7b,
       u_PoliLobinho_db_classe_atual, u_PoliLobinho_db_estado_7b, u_PoliLobinho_db_jogador_atual,
       u_PoliLobinho_db_protegido_7b, u_PoliLobinho_db_seed_7b;

  Button #(.activeLow("true")) button_1 (.out(button_1_out[0]));
  Button #(.activeLow("true")) button_2 (.out(button_1_out[1]));
  Button #(.activeLow("true")) button_3 (.out(button_1_out[2]));
  Button #(.activeLow("true")) button_4 (.out(button_1_out[3]));
  Button #(.activeLow("true")) button_5 (.out(button_1_out[4]));
  Button #(.activeLow("true")) button_6 (.out(button_6_out));
  Button #(.activeLow("true")) button_7 (.out(button_7_out));
  Button #(.activeLow("true")) button_8 (.out(button_8_out));
  Button #(.activeLow("true")) button_9 (.out(button_9_out));
  PoliLobinho #(.applicationType("IVERILOG"), .CodeFile("C:\\Users\\anton\\Documents\\PoliLobinho\\digital.v")) u_PoliLobinho (
    .clock(clk), .pular(button_6_out), .botoes_jogadores(button_1_out), .reset(button_7_out),
    .jogar(button_8_out), .passa(button_9_out), .db_classe_atual(u_PoliLobinho_db_classe_atual),
    .db_jogador_atual(u_PoliLobinho_db_jogador_atual), .db_estado_7b(u_PoliLobinho_db_estado_7b),
    .db_seed_7b(u_PoliLobinho_db_seed_7b), .db_atacado_7b(u_PoliLobinho_db_atacado_7b),
    .db_protegido_7b(u_PoliLobinho_db_protegido_7b), .db_jogador_escolhido(out_2), .db_mortes(out_3),
    .db_clock(u_PoliLobinho_db_clock));  // open: ganhamo, votaram
  LED led_1 (.in(u_PoliLobinho_db_clock));
  assign not_1_out = ~u_PoliLobinho_db_atacado_7b;  // Not not_1, 7 bits wide
  Seven_Seg seven_seg_1 (
    .a(not_1_out[0]), .b(not_1_out[1]), .c(not_1_out[2]), .d(not_1_out[3]), .e(not_1_out[4]),
    .f(not_1_out[5]), .g(not_1_out[6]), .dp(1'b0));
  assign not_2_out = ~u_PoliLobinho_db_classe_atual;  // Not not_2, 7 bits wide
  Seven_Seg seven_seg_2 (
    .a(not_2_out[0]), .b(not_2_out[1]), .c(not_2_out[2]), .d(not_2_out[3]), .e(not_2_out[4]),
    .f(not_2_out[5]), .g(not_2_out[6]), .dp(1'b0));
  assign not_3_out = ~u_PoliLobinho_db_seed_7b;  // Not not_3, 7 bits wide
  Seven_Seg seven_seg_3 (
    .a(not_3_out[0]), .b(not_3_out[1]), .c(not_3_out[2]), .d(not_3_out[3]), .e(not_3_out[4]),
    .f(not_3_out[5]), .g(not_3_out[6]), .dp(1'b0));
  assign not_4_out = ~u_PoliLobinho_db_protegido_7b;  // Not not_4, 7 bits wide
  Seven_Seg seven_seg_4 (
    .a(not_4_out[0]), .b(not_4_out[1]), .c(not_4_out[2]), .d(not_4_out[3]), .e(not_4_out[4]),
    .f(not_4_out[5]), .g(not_4_out[6]), .dp(1'b0));
  assign not_5_out = ~u_PoliLobinho_db_jogador_atual;  // Not not_5, 7 bits wide
  Seven_Seg seven_seg_5 (
    .a(not_5_out[0]), .b(not_5_out[1]), .c(not_5_out[2]), .d(not_5_out[3]), .e(not_5_out[4]),
    .f(not_5_out[5]), .g(not_5_out[6]), .dp(1'b0));
  assign not_6_out = ~u_PoliLobinho_db_estado_7b;  // Not not_6, 7 bits wide
  Seven_Seg seven_seg_6 (
    .a(not_6_out[0]), .b(not_6_out[1]), .c(not_6_out[2]), .d(not_6_out[3]), .e(not_6_out[4]),
    .f(not_6_out[5]), .g(not_6_out[6]), .dp(1'b0));

  // Notes on the sheet:
  //   clk: Hz: 1000
  //   Atacado
  //   Classe
  //   Seed
  //   Protegido
  //   Jogador
  //   Estado
endmodule
